# Fritzing sketch handProto (saved by Fritzing 0.9.3b)
breadboards: 1

parts:
  Part1 = Arduino Uno (Rev3)
  Part2 = Arduino Uno (Rev3)
  J1 = Basic Servo
  VCC1 = Battery
  J2 = Basic Force Sensing Resistor (FSR) [package=THT]
  R1 = Resistor [tolerance=±5% resistance=220 package="0603 [SMD]"]

nets:
  N1: Part1.A0, J2.pin_0, R1.Pin_0
  N2: Part1.D10_PWM/SS, Part2.D11_PWM/MOSI
  N3: Part1.D11_PWM/MOSI, Part2.D10_PWM/SS
  5V: Part1.5V, Part2.5V, J2.pin_1
  GND: Part1.GND, Part2.GND, J1.gnd, VCC1.-, R1.Pin_1
  N4: Part2.D9_PWM, J1.pulse
