# Fritzing sketch roboticHand (saved by Fritzing 0.9.3b)
breadboards: 1

parts:
  Part1 = Arduino Uno (Rev3)
  finger_1 = Basic Flex Resistor
  finger_2 = Resistor [tolerance=±5% resistance=10k package=THT]
  finger_3 = Resistor [tolerance=±5% resistance=10k package=THT]
  finger_1_2 = Resistor [tolerance=±5% resistance=10k package=THT]
  finger_4 = Resistor [tolerance=±5% resistance=10k package=THT]
  finger_5 = Resistor [tolerance=±5% resistance=10k package=THT]
  finger_2_2 = Basic Flex Resistor
  finger_3_2 = Basic Flex Resistor
  finger_4_2 = Basic Flex Resistor
  finger_5_2 = Basic Flex Resistor

nets:
  N1: Part1.A0, finger_1.pin_1, finger_1_2.Pin_1
  N2: Part1.A1, finger_2.Pin_1, finger_2_2.pin_1
  N3: Part1.A2, finger_3.Pin_1, finger_3_2.pin_1
  N4: Part1.A3, finger_4.Pin_1, finger_4_2.pin_1
  N5: Part1.GND, finger_2.Pin_0, finger_3.Pin_0, finger_1_2.Pin_0, finger_4.Pin_0, finger_5.Pin_0
  N6: Part1.A4/SDA, finger_5.Pin_1, finger_5_2.pin_1
  N7: Part1.3V3, finger_1.Pin_2, finger_2_2.Pin_2, finger_3_2.Pin_2, finger_4_2.Pin_2, finger_5_2.Pin_2
